// Logisim project JOB02.circ as structural Verilog
module HA (
  input  a,
  input  b,
  output s,
  output c
);

  xor xor_1 (s, a, b);
  and and_1 (c, a, b);
endmodule

module FA (
  input  A,
  input  B,
  input  C,
  output S,
  output Co
);

  wire ha_1_c, ha_1_s, ha_2_c;

  HA ha_1 (.a(A), .b(B), .s(ha_1_s), .c(ha_1_c));
  HA ha_2 (.a(ha_1_s), .b(C), .s(S), .c(ha_2_c));
  or or_1 (Co, ha_2_c, ha_1_c);
endmodule

module Add_4bits (
  input  [3:0] A,
  input  in_2,
  input  [3:0] B,
  output C,
  output [3:0] Sum
);

  wire fa_1_co, fa_2_co, fa_3_co;

  FA fa_1 (.A(A[0]), .B(B[0]), .C(in_2), .S(Sum[0]), .Co(fa_1_co));
  FA fa_2 (.A(A[1]), .B(B[1]), .C(fa_1_co), .S(Sum[1]), .Co(fa_2_co));
  FA fa_3 (.A(A[2]), .B(B[2]), .C(fa_2_co), .S(Sum[2]), .Co(fa_3_co));
  FA fa_4 (.A(A[3]), .B(B[3]), .C(fa_3_co), .S(Sum[3]), .Co(C));
endmodule
