// Logisim project JOB03.circ as structural Verilog
module HA (
  input  a,
  input  b,
  output s,
  output c
);

  xor xor_1 (s, a, b);
  and and_1 (c, a, b);
endmodule

module FA (
  input  A,
  input  B,
  input  C,
  output S,
  output Co
);

  wire ha_1_c, ha_1_s, ha_2_c;

  HA ha_1 (.a(A), .b(B), .s(ha_1_s), .c(ha_1_c));
  HA ha_2 (.a(ha_1_s), .b(C), .s(S), .c(ha_2_c));
  or or_1 (Co, ha_2_c, ha_1_c);
endmodule

module Add_4bits (
  input  [3:0] A,
  input  in_2,
  input  [3:0] B,
  output C,
  output [3:0] Sum
);

  wire fa_1_co, fa_2_co, fa_3_co;

  FA fa_1 (.A(A[0]), .B(B[0]), .C(in_2), .S(Sum[0]), .Co(fa_1_co));
  FA fa_2 (.A(A[1]), .B(B[1]), .C(fa_1_co), .S(Sum[1]), .Co(fa_2_co));
  FA fa_3 (.A(A[2]), .B(B[2]), .C(fa_2_co), .S(Sum[2]), .Co(fa_3_co));
  FA fa_4 (.A(A[3]), .B(B[3]), .C(fa_3_co), .S(Sum[3]), .Co(C));
endmodule

module HS (
  input  a,
  input  b,
  output d,
  output br
);

  wire not_1_out;

  not not_1 (not_1_out, a);
  xor xor_1 (d, a, b);
  and and_1 (br, not_1_out, b);
endmodule

module FS (
  input  A,
  input  B,
  input  Rr,
  output D,
  output Rro
);

  wire hs_1_br, hs_1_d, hs_2_br;

  HS hs_1 (.a(A), .b(B), .d(hs_1_d), .br(hs_1_br));
  HS hs_2 (.a(hs_1_d), .b(Rr), .d(D), .br(hs_2_br));
  or or_1 (Rro, hs_2_br, hs_1_br);
endmodule

module Sub_4bits (
  input  [3:0] A,
  input  in_2,
  input  [3:0] B,
  output Br,
  output [3:0] D
);

  wire fs_1_rro, fs_2_rro, fs_3_rro;

  FS fs_1 (.A(A[0]), .B(B[0]), .Rr(in_2), .D(D[0]), .Rro(fs_1_rro));
  FS fs_2 (.A(A[1]), .B(B[1]), .Rr(fs_1_rro), .D(D[1]), .Rro(fs_2_rro));
  FS fs_3 (.A(A[2]), .B(B[2]), .Rr(fs_2_rro), .D(D[2]), .Rro(fs_3_rro));
  FS fs_4 (.A(A[3]), .B(B[3]), .Rr(fs_3_rro), .D(D[3]), .Rro(Br));
endmodule

module add_sub_4bits (
  input  [3:0] A,
  input  S,
  input  [3:0] B,
  output C,
  output [3:0] Result
);

  wire fa_1_co, fa_2_co, fa_3_co, xor_1_out, xor_2_out, xor_3_out, xor_4_out;

  xor xor_1 (xor_1_out, S, B[0]);
  FA fa_1 (.A(A[0]), .B(xor_1_out), .C(S), .S(Result[0]), .Co(fa_1_co));
  xor xor_2 (xor_2_out, S, B[1]);
  FA fa_2 (.A(A[1]), .B(xor_2_out), .C(fa_1_co), .S(Result[1]), .Co(fa_2_co));
  xor xor_3 (xor_3_out, S, B[2]);
  FA fa_3 (.A(A[2]), .B(xor_3_out), .C(fa_2_co), .S(Result[2]), .Co(fa_3_co));
  xor xor_4 (xor_4_out, S, B[3]);
  FA fa_4 (.A(A[3]), .B(xor_4_out), .C(fa_3_co), .S(Result[3]), .Co(C));
endmodule
