// Logisim project JOB04.circ as structural Verilog
module HA (
  input  a,
  input  b,
  output s,
  output c
);

  xor xor_1 (s, a, b);
  and and_1 (c, a, b);
endmodule

module FA (
  input  A,
  input  B,
  input  C,
  output S,
  output Co
);

  wire ha_1_c, ha_1_s, ha_2_c;

  HA ha_1 (.a(A), .b(B), .s(ha_1_s), .c(ha_1_c));
  HA ha_2 (.a(ha_1_s), .b(C), .s(S), .c(ha_2_c));
  or or_1 (Co, ha_2_c, ha_1_c);
endmodule

module Add_4bits (
  input  [3:0] A,
  input  in_2,
  input  [3:0] B,
  output C,
  output [3:0] Sum
);

  wire fa_1_co, fa_2_co, fa_3_co;

  FA fa_1 (.A(A[0]), .B(B[0]), .C(in_2), .S(Sum[0]), .Co(fa_1_co));
  FA fa_2 (.A(A[1]), .B(B[1]), .C(fa_1_co), .S(Sum[1]), .Co(fa_2_co));
  FA fa_3 (.A(A[2]), .B(B[2]), .C(fa_2_co), .S(Sum[2]), .Co(fa_3_co));
  FA fa_4 (.A(A[3]), .B(B[3]), .C(fa_3_co), .S(Sum[3]), .Co(C));
endmodule

module HS (
  input  a,
  input  b,
  output d,
  output br
);

  wire not_1_out;

  not not_1 (not_1_out, a);
  xor xor_1 (d, a, b);
  and and_1 (br, not_1_out, b);
endmodule

module FS (
  input  A,
  input  B,
  input  Rr,
  output D,
  output Rro
);

  wire hs_1_br, hs_1_d, hs_2_br;

  HS hs_1 (.a(A), .b(B), .d(hs_1_d), .br(hs_1_br));
  HS hs_2 (.a(hs_1_d), .b(Rr), .d(D), .br(hs_2_br));
  or or_1 (Rro, hs_2_br, hs_1_br);
endmodule

module Sub_4bits (
  input  [3:0] A,
  input  in_2,
  input  [3:0] B,
  output Br,
  output [3:0] D
);

  wire fs_1_rro, fs_2_rro, fs_3_rro;

  FS fs_1 (.A(A[0]), .B(B[0]), .Rr(in_2), .D(D[0]), .Rro(fs_1_rro));
  FS fs_2 (.A(A[1]), .B(B[1]), .Rr(fs_1_rro), .D(D[1]), .Rro(fs_2_rro));
  FS fs_3 (.A(A[2]), .B(B[2]), .Rr(fs_2_rro), .D(D[2]), .Rro(fs_3_rro));
  FS fs_4 (.A(A[3]), .B(B[3]), .Rr(fs_3_rro), .D(D[3]), .Rro(Br));
endmodule

module add_sub_4bits (
  input  [3:0] A,
  input  S,
  input  [3:0] B,
  output C,
  output [3:0] Result
);

  wire fa_1_co, fa_2_co, fa_3_co, xor_1_out, xor_2_out, xor_3_out, xor_4_out;

  xor xor_1 (xor_1_out, S, B[0]);
  FA fa_1 (.A(A[0]), .B(xor_1_out), .C(S), .S(Result[0]), .Co(fa_1_co));
  xor xor_2 (xor_2_out, S, B[1]);
  FA fa_2 (.A(A[1]), .B(xor_2_out), .C(fa_1_co), .S(Result[1]), .Co(fa_2_co));
  xor xor_3 (xor_3_out, S, B[2]);
  FA fa_3 (.A(A[2]), .B(xor_3_out), .C(fa_2_co), .S(Result[2]), .Co(fa_3_co));
  xor xor_4 (xor_4_out, S, B[3]);
  FA fa_4 (.A(A[3]), .B(xor_4_out), .C(fa_3_co), .S(Result[3]), .Co(C));
endmodule

module comp (
  input  A,
  input  B,
  output Y_eq,
  output Y_neq,
  output Y_a_b,
  output Y_b_a
);

  wire not_1_out, not_2_out;

  xor xor_1 (Y_neq, A, B);
  and and_1 (Y_a_b, A, not_1_out);
  not not_1 (not_1_out, B);
  not not_2 (not_2_out, A);
  and and_2 (Y_b_a, not_2_out, B);
  xnor xnor_1 (Y_eq, A, B);
endmodule

module encode (
  input  D7,
  input  D6,
  input  D5,
  input  D4,
  input  D3,
  input  D2,
  input  D1,
  input  D0,
  output Y2_C,
  output Y1_B,
  output Y0_A
);

  or or_1 (Y2_C, D4, D5, D6, D7);
  or or_2 (Y1_B, D2, D3, D6, D7);
  or or_3 (Y0_A, D1, D3, D5, D7);
endmodule

module decode (
  input  Y2_C,
  input  Y1_B,
  input  Y0_A,
  output D7,
  output D6,
  output D5,
  output D4,
  output D3,
  output D2,
  output D1,
  output D0
);

  wire not_1_out, not_2_out, not_3_out;

  not not_1 (not_1_out, Y2_C);
  not not_2 (not_2_out, Y1_B);
  not not_3 (not_3_out, Y0_A);
  and and_1 (D7, Y2_C, Y1_B, Y0_A);
  and and_2 (D6, Y2_C, Y1_B, not_3_out);
  and and_3 (D5, Y2_C, not_2_out, Y0_A);
  and and_4 (D4, Y2_C, not_2_out, not_3_out);
  and and_5 (D3, not_1_out, Y1_B, Y0_A);
  and and_6 (D2, not_1_out, Y1_B, not_3_out);
  and and_7 (D1, not_1_out, not_2_out, Y0_A);
  and and_8 (D0, not_1_out, not_2_out, not_3_out);
endmodule

module Mux (
  input  Data0,
  input  Data1,
  input  Data2,
  input  Data3,
  input  S1,
  input  S0,
  output Out_Data
);

  wire and_1_out, and_2_out, and_3_out, and_4_out, not_1_out, not_2_out;

  not not_1 (not_1_out, S1);
  not not_2 (not_2_out, S0);
  and and_1 (and_1_out, Data0, not_1_out, not_2_out);
  and and_2 (and_2_out, Data1, not_1_out, S0);
  and and_3 (and_3_out, Data2, S1, not_2_out);
  and and_4 (and_4_out, Data3, S1, S0);
  or or_1 (Out_Data, and_1_out, and_2_out, and_3_out, and_4_out);
endmodule

module Demux (
  input  Data_in,
  input  S1,
  input  S0,
  output Out3,
  output Out2,
  output Out1,
  output Out0
);

  wire not_1_out, not_2_out;

  not not_1 (not_1_out, S1);
  not not_2 (not_2_out, S0);
  and and_1 (Out3, Data_in, S1, S0);
  and and_2 (Out2, Data_in, S1, not_2_out);
  and and_3 (Out1, Data_in, not_1_out, S0);
  and and_4 (Out0, Data_in, not_1_out, not_2_out);
endmodule
