// Logisim project JOB06.circ as structural Verilog
module latch (
  input  R,
  input  S,
  output Q,
  output Qbar
);

  nor nor_1 (Q, R, Qbar);
  nor nor_2 (Qbar, Q, S);
endmodule

module RSFF (
  input  R,
  input  CLK,
  input  S,
  output Q,
  output Qbar
);

  wire and_1_out, and_2_out;

  and and_1 (and_1_out, R, CLK);
  and and_2 (and_2_out, CLK, S);
  nor nor_1 (Q, and_1_out, Qbar);
  nor nor_2 (Qbar, Q, and_2_out);
endmodule

module JKFF (
  input  K,
  input  CLK,
  input  J,
  output Q,
  output Qbar
);

  wire and_1_out, and_2_out;

  and and_1 (and_1_out, K, Q, CLK);
  and and_2 (and_2_out, CLK, Qbar, J);
  nor nor_1 (Q, and_1_out, Qbar);
  nor nor_2 (Qbar, Q, and_2_out);
endmodule

module DFF (
  input  CLK,
  input  D,
  output Q,
  output Qbar
);

  wire and_1_out, and_2_out, not_1_out;

  not not_1 (not_1_out, D);
  and and_1 (and_1_out, not_1_out, Q, CLK);
  and and_2 (and_2_out, CLK, Qbar, D);
  nor nor_1 (Q, and_1_out, Qbar);
  nor nor_2 (Qbar, Q, and_2_out);
endmodule

module TFF (
  input  CLK,
  input  D,
  output Q,
  output Qbar
);

  wire and_1_out, and_2_out;

  and and_1 (and_1_out, D, Q, CLK);
  and and_2 (and_2_out, CLK, Qbar, D);
  nor nor_1 (Q, and_1_out, Qbar);
  nor nor_2 (Qbar, Q, and_2_out);
endmodule

module test (
  input  in_1,
  input  in_2,
  input  in_3,
  input  in_4,
  input  in_5,
  input  in_6,
  input  in_7,
  input  in_8,
  input  in_9,
  input  in_10,
  input  in_11,
  input  in_12,
  input  in_13,
  input  in_14,
  output out_15,
  output out_16,
  output out_17,
  output out_18,
  output out_19,
  output out_20
);

  wire not_1_out;

  J_K_Flip_Flop j_k_ff_1 (.J(in_7), .K(not_1_out), .clk(in_11), .Q(out_17));  // open: Qn, preset, reset
  not not_1 (not_1_out, in_7);
  S_R_Flip_Flop s_r_ff_1 (.S(in_1), .R(in_3), .clk(in_5), .Q(out_15));  // open: reset, Qn, preset
  J_K_Flip_Flop j_k_ff_2 (.J(in_2), .K(in_4), .clk(in_6), .Q(out_16));  // open: Qn, preset, reset
  D_Flip_Flop d_ff_1 (.D(in_8), .clk(in_12), .Q(out_18));  // open: Qn, preset, reset
  J_K_Flip_Flop j_k_ff_3 (.J(in_9), .K(in_9), .clk(in_13), .Q(out_19));  // open: Qn, preset, reset
  T_Flip_Flop t_ff_1 (.T(in_10), .clk(in_14), .Q(out_20));  // open: Qn, reset, preset
endmodule

module siso (
  input  indata,
  output outdata
);

  wire CLK_out, d_ff_1_q, d_ff_2_q, d_ff_3_q;

  Clock CLK (.out(CLK_out));
  D_Flip_Flop d_ff_1 (.D(indata), .clk(CLK_out), .Q(d_ff_1_q));  // open: Qn, preset, reset
  D_Flip_Flop d_ff_2 (.D(d_ff_1_q), .clk(CLK_out), .Q(d_ff_2_q));  // open: Qn, preset, reset
  D_Flip_Flop d_ff_3 (.D(d_ff_2_q), .clk(CLK_out), .Q(d_ff_3_q));  // open: Qn, preset, reset
  D_Flip_Flop d_ff_4 (.D(d_ff_3_q), .clk(CLK_out), .Q(outdata));  // open: Qn, preset, reset
endmodule

module sipo (
  input  indata,
  output out0,
  output out1,
  output out2,
  output out3
);

  wire CLK_out;

  Clock CLK (.out(CLK_out));
  D_Flip_Flop d_ff_1 (.D(indata), .clk(CLK_out), .Q(out0));  // open: Qn, preset, reset
  D_Flip_Flop d_ff_2 (.D(out0), .clk(CLK_out), .Q(out1));  // open: Qn, preset, reset
  D_Flip_Flop d_ff_3 (.D(out1), .clk(CLK_out), .Q(out2));  // open: Qn, preset, reset
  D_Flip_Flop d_ff_4 (.D(out2), .clk(CLK_out), .Q(out3));  // open: Qn, preset, reset
endmodule

module piso (
  input  in1,
  input  in2,
  input  in3,
  input  in4,
  input  SH_LD,
  output result
);

  wire and_1_out, and_2_out, and_3_out, and_4_out, and_5_out, and_6_out, CLK_out, d_ff_1_q, d_ff_2_q,
       d_ff_3_q, not_1_out, or_1_out, or_2_out, or_3_out;

  not not_1 (not_1_out, SH_LD);
  Clock CLK (.out(CLK_out));
  D_Flip_Flop d_ff_1 (.D(in1), .clk(CLK_out), .Q(d_ff_1_q));  // open: Qn, preset, reset
  and and_1 (and_1_out, d_ff_1_q, SH_LD);
  and and_2 (and_2_out, not_1_out, in2);
  or or_1 (or_1_out, and_1_out, and_2_out);
  D_Flip_Flop d_ff_2 (.D(or_1_out), .clk(CLK_out), .Q(d_ff_2_q));  // open: Qn, preset, reset
  and and_3 (and_3_out, d_ff_2_q, SH_LD);
  or or_2 (or_2_out, and_3_out, and_4_out);
  and and_4 (and_4_out, not_1_out, in3);
  D_Flip_Flop d_ff_3 (.D(or_2_out), .clk(CLK_out), .Q(d_ff_3_q));  // open: Qn, preset, reset
  and and_5 (and_5_out, d_ff_3_q, SH_LD);
  and and_6 (and_6_out, not_1_out, in4);
  or or_3 (or_3_out, and_5_out, and_6_out);
  D_Flip_Flop d_ff_4 (.D(or_3_out), .clk(CLK_out), .Q(result));  // open: Qn, preset, reset
endmodule

module pipo (
  input  in0,
  input  in1,
  input  in2,
  input  in3,
  output out0,
  output out1,
  output out2,
  output out3
);

  wire CLK_out;

  Clock CLK (.out(CLK_out));
  D_Flip_Flop d_ff_1 (.D(in0), .clk(CLK_out), .Q(out0));  // open: Qn, preset, reset
  D_Flip_Flop d_ff_2 (.D(in1), .clk(CLK_out), .Q(out1));  // open: Qn, preset, reset
  D_Flip_Flop d_ff_3 (.D(in2), .clk(CLK_out), .Q(out2));  // open: Qn, preset, reset
  D_Flip_Flop d_ff_4 (.D(in3), .clk(CLK_out), .Q(out3));  // open: Qn, preset, reset
endmodule

module recirc (
  input  control,
  input  ind,
  output outd
);

  wire and_1_out, and_2_out, CLK_out, d_ff_1_q, d_ff_2_q, d_ff_3_q, not_1_out, or_1_out;

  not not_1 (not_1_out, control);
  and and_1 (and_1_out, outd, not_1_out);
  and and_2 (and_2_out, control, ind);
  Clock CLK (.out(CLK_out));
  or or_1 (or_1_out, and_1_out, and_2_out);
  D_Flip_Flop d_ff_1 (.D(or_1_out), .clk(CLK_out), .Q(d_ff_1_q));  // open: Qn, preset, reset
  D_Flip_Flop d_ff_2 (.D(d_ff_1_q), .clk(CLK_out), .Q(d_ff_2_q));  // open: Qn, preset, reset
  D_Flip_Flop d_ff_3 (.D(d_ff_2_q), .clk(CLK_out), .Q(d_ff_3_q));  // open: Qn, preset, reset
  D_Flip_Flop d_ff_4 (.D(d_ff_3_q), .clk(CLK_out), .Q(outd));  // open: Qn, preset, reset

  // Notes on the sheet:
  //   1.직렬데이터 입력
  //   0.순환 데이터 입력
endmodule

module dual (
  input  SLI,
  input  SRI,
  input  R_Lbar,
  output out0,
  output out1,
  output out2,
  output out3,
  output SLO,
  output SRO
);

  wire clock_1_out, mux_1_y, mux_2_y, mux_3_y, mux_4_y;

  Clock clock_1 (.out(clock_1_out));
  MUX mux_1 (.SLI(out1), .SRI(SRI), .R_Lbar(R_Lbar), .Y(mux_1_y));
  D_Flip_Flop d_ff_1 (.D(mux_1_y), .clk(clock_1_out), .Q(out0));  // open: Qn, preset, reset
  MUX mux_2 (.SLI(out2), .SRI(out0), .R_Lbar(R_Lbar), .Y(mux_2_y));
  D_Flip_Flop d_ff_2 (.D(mux_2_y), .clk(clock_1_out), .Q(out1));  // open: Qn, preset, reset
  MUX mux_3 (.SLI(out3), .SRI(out1), .R_Lbar(R_Lbar), .Y(mux_3_y));
  D_Flip_Flop d_ff_3 (.D(mux_3_y), .clk(clock_1_out), .Q(out2));  // open: Qn, preset, reset
  MUX mux_4 (.SLI(SLI), .SRI(out2), .R_Lbar(R_Lbar), .Y(mux_4_y));
  D_Flip_Flop d_ff_4 (.D(mux_4_y), .clk(clock_1_out), .Q(out3));  // open: Qn, preset, reset

  assign SLO = out0;
  assign SRO = out3;
endmodule

module MUX (
  input  SLI,
  input  SRI,
  input  R_Lbar,
  output Y
);

  wire and_1_out, and_2_out, not_1_out;

  not not_1 (not_1_out, R_Lbar);
  and and_1 (and_1_out, SLI, not_1_out);
  and and_2 (and_2_out, R_Lbar, SRI);
  or or_1 (Y, and_1_out, and_2_out);
endmodule
