// Logisim project JOB_1000.circ as structural Verilog: 20 circuits, main circuit main
module main (
  input  A0,
  input  B0,
  input  Bi,
  input  [3:0] A_4bits,
  input  selector,
  input  [3:0] B_4bits,
  input  A1,
  input  B1,
  input  Ci,
  input  \_1_감산기 ,
  input  in_11,
  input  in_12,
  input  [3:0] in_13,
  input  in_14,
  input  [3:0] in_15,
  input  in_16,
  input  in_17,
  input  in_18,
  input  in_19,
  input  in_20,
  input  in_21,
  output D,
  output Bo,
  output \C_0_음수 ,
  output [3:0] S_4bits,
  output S,
  output Co,
  output out_28,
  output out_29,
  output [3:0] out_30,
  output out_31,
  output out_32,
  output out_33,
  output out_34,
  output out_35,
  output out_36,
  output out_37,
  output out_38,
  output out_39,
  output out_40,
  output out_41,
  output out_42,
  output out_43,
  output out_44,
  output out_45,
  output out_46,
  output out_47
);

  wire clock_1_out, clock_2_out, clock_3_out, clock_4_out, clock_5_out, not_1_out;

  Clock clock_1 (.out(clock_1_out));
  Clock clock_2 (.out(clock_2_out));
  J_K_Flip_Flop j_k_ff_1 (.J(in_16), .K(in_17), .clk(clock_1_out), .Q(out_36), .Qn(out_39));  // open: preset, reset
  J_K_Flip_Flop j_k_ff_2 (.J(in_18), .K(in_18), .clk(clock_2_out), .Q(out_40), .Qn(out_42));  // open: preset, reset
  T_Flip_Flop t_ff_1 (.T(in_20), .clk(clock_3_out), .Q(out_44), .Qn(out_46));  // open: reset, preset
  Clock clock_3 (.out(clock_3_out));
  FS fs_1 (.A(A0), .B(B0), .Bi(Bi), .D(D), .Bo(Bo));
  FA fa_1 (.A(A1), .B(B1), .Ci(Ci), .S(S), .Co(Co));
  Clock clock_4 (.out(clock_4_out));
  Clock clock_5 (.out(clock_5_out));
  J_K_Flip_Flop j_k_ff_3 (.J(in_19), .K(not_1_out), .clk(clock_4_out), .Q(out_41), .Qn(out_43));  // open: preset, reset
  not not_1 (not_1_out, in_19);
  D_Flip_Flop d_ff_1 (.D(in_21), .clk(clock_5_out), .Q(out_45), .Qn(out_47));  // open: preset, reset
  Subtractor #(.width(4)) subtractor_1 (.a(in_13), .b(in_15), .out(out_30), .bin(\_1_감산기 ), .bout(out_33));
  Parrel_Adder_Substract parrel_adder_substract_1 (
    .A_4(A_4bits), .selector(selector), .B_4(B_4bits), .C(\C_0_음수 ), .S_4(S_4bits));  // open: in_3, in_2, in_1, out_8, out_7, out_11
  decode_3to8 decode_3to8_1 (
    .D2(in_11), .D1(in_12), .D0(in_14), .Y0(out_28), .Y1(out_29), .Y2(out_31), .Y3(out_32), .Y4(out_34),
    .Y5(out_35), .Y6(out_37), .Y7(out_38));

  // Notes on the sheet:
  //   selector
  //   0:가산기
  //   C:1-양수
  //   감산기일경우
  //   감산기로 동작할 때
  //   2의 보수값으로 나옴
endmodule

module basic_gates (
  input  A,
  input  B,
  output Y_and,
  output Y_or,
  output Y_not,
  output Y_nand,
  output Y_nor,
  output Y_xor,
  output Y_xnor,
  output Y_buff
);

  not not_1 (Y_not, A);
  buf buffer_1 (Y_buff, A);
  and and_1 (Y_and, A, B);
  or or_1 (Y_or, A, B);
  nand nand_1 (Y_nand, A, B);
  nor nor_1 (Y_nor, A, B);
  xor xor_1 (Y_xor, A, B);
  xnor xnor_1 (Y_xnor, A, B);
endmodule

module HA (
  input  A,
  input  B,
  output S,
  output Ci
);

  xor xor_1 (S, A, B);
  and and_1 (Ci, A, B);

  // Notes on the sheet:
  //   가산기
endmodule

module FA (
  input  A,
  input  B,
  input  Ci,
  output S,
  output Co
);

  wire ha_1_ci, ha_1_s, ha_2_ci;

  HA ha_1 (.A(A), .B(B), .S(ha_1_s), .Ci(ha_1_ci));
  HA ha_2 (.A(ha_1_s), .B(Ci), .S(S), .Ci(ha_2_ci));
  or or_1 (Co, ha_2_ci, ha_1_ci);
endmodule

module Adder_4bits (
  input  in_1,
  input  [3:0] in_2,
  input  [3:0] in_3,
  input  [3:0] A_4,
  input  in_5,
  input  [3:0] B_4,
  output [3:0] out_7,
  output out_8,
  output C,
  output [3:0] S_4
);

  wire fa_1_co, fa_2_co, fa_3_co;

  Adder #(.width(4)) adder_1 (.a(in_2), .b(in_3), .out(out_7), .cin(in_1), .cout(out_8));
  FA fa_1 (.A(A_4[0]), .B(B_4[0]), .Ci(in_5), .S(S_4[0]), .Co(fa_1_co));
  FA fa_2 (.A(A_4[1]), .B(B_4[1]), .Ci(fa_1_co), .S(S_4[1]), .Co(fa_2_co));
  FA fa_3 (.A(A_4[2]), .B(B_4[2]), .Ci(fa_2_co), .S(S_4[2]), .Co(fa_3_co));
  FA fa_4 (.A(A_4[3]), .B(B_4[3]), .Ci(fa_3_co), .S(S_4[3]), .Co(C));
endmodule

module HS (
  input  A,
  input  B,
  output D,
  output Bi
);

  wire not_1_out;

  not not_1 (not_1_out, A);
  xor xor_1 (D, A, B);
  and and_1 (Bi, not_1_out, B);

  // Notes on the sheet:
  //   감산기
endmodule

module FS (
  input  A,
  input  B,
  input  Bi,
  output D,
  output Bo
);

  wire hs_1_bi, hs_1_d, hs_2_bi;

  HS hs_1 (.A(A), .B(B), .D(hs_1_d), .Bi(hs_1_bi));
  HS hs_2 (.A(hs_1_d), .B(Bi), .D(D), .Bi(hs_2_bi));
  or or_1 (Bo, hs_2_bi, hs_1_bi);
endmodule

module Substract_4bits (
  input  in_1,
  input  [3:0] in_2,
  input  [3:0] in_3,
  input  [3:0] in_4,
  input  in_5,
  input  [3:0] in_6,
  output [3:0] out_7,
  output out_8,
  output [3:0] out_9,
  output out_10
);

  wire fs_1_bo, fs_2_bo, fs_3_bo;

  Subtractor #(.width(4)) subtractor_1 (.a(in_2), .b(in_3), .out(out_7), .bin(in_1), .bout(out_8));
  FS fs_1 (.A(in_4[0]), .B(in_6[0]), .Bi(in_5), .D(out_9[0]), .Bo(fs_1_bo));
  FS fs_2 (.A(in_4[1]), .B(in_6[1]), .Bi(fs_1_bo), .D(out_9[1]), .Bo(fs_2_bo));
  FS fs_3 (.A(in_4[2]), .B(in_6[2]), .Bi(fs_2_bo), .D(out_9[2]), .Bo(fs_3_bo));
  FS fs_4 (.A(in_4[3]), .B(in_6[3]), .Bi(fs_3_bo), .D(out_9[3]), .Bo(out_10));
endmodule

module Parrel_Adder_Substract (
  input  in_1,
  input  [3:0] in_2,
  input  [3:0] in_3,
  input  [3:0] A_4,
  input  selector,
  input  [3:0] B_4,
  output [3:0] out_7,
  output out_8,
  output C,
  output [3:0] S_4,
  output [3:0] out_11
);

  wire fa_1_co, fa_2_co, fa_3_co, xor_1_out, xor_2_out, xor_4_out, xor_5_out;
  wire [3:0] buffer_1_out, xor_3_out;

  buf buffer_1 (buffer_1_out[0], in_1);
  buf buffer_2 (buffer_1_out[1], in_1);
  buf buffer_3 (buffer_1_out[2], in_1);
  buf buffer_4 (buffer_1_out[3], in_1);
  xor xor_1 (xor_1_out, selector, B_4[0]);
  FA fa_1 (.A(A_4[0]), .B(xor_1_out), .Ci(selector), .S(out_11[0]), .Co(fa_1_co));
  xor xor_2 (xor_2_out, selector, B_4[1]);
  Adder #(.width(4)) adder_1 (.a(in_2), .b(xor_3_out), .out(out_7), .cin(in_1), .cout(out_8));
  assign xor_3_out = buffer_1_out ^ in_3;  // XOR_Gate xor_3, 4 bits wide
  FA fa_2 (.A(A_4[1]), .B(xor_2_out), .Ci(fa_1_co), .S(out_11[1]), .Co(fa_2_co));
  FA fa_3 (.A(A_4[2]), .B(xor_4_out), .Ci(fa_2_co), .S(out_11[2]), .Co(fa_3_co));
  xor xor_4 (xor_4_out, selector, B_4[2]);
  xor xor_5 (xor_5_out, selector, B_4[3]);
  FA fa_4 (.A(A_4[3]), .B(xor_5_out), .Ci(fa_3_co), .S(out_11[3]), .Co(C));

  assign S_4 = out_11;
endmodule

module comp_1bit (
  input  A,
  input  B,
  output Y_same,
  output Y_notsame,
  output Y_abt,
  output Y_alt
);

  wire not_1_out, not_2_out;

  not not_1 (not_1_out, B);
  not not_2 (not_2_out, A);
  xnor xnor_1 (Y_same, A, B);
  xor xor_1 (Y_notsame, A, B);
  and and_1 (Y_abt, A, not_1_out);
  and and_2 (Y_alt, not_2_out, B);
endmodule

module comp_2bits (
  input  [1:0] A,
  input  [1:0] B,
  output Y_same,
  output Y_notsame,
  output Y_abt,
  output Y_alt
);

  wire and_1_out, and_2_out, and_3_out, and_4_out, and_5_out, and_6_out, not_1_out, not_2_out, not_3_out,
       not_4_out, not_5_out, not_6_out, not_7_out, not_8_out, xnor_1_out, xnor_2_out, xor_1_out, xor_2_out;

  not not_1 (not_1_out, B[1]);
  not not_2 (not_2_out, B[0]);
  not not_3 (not_3_out, B[1]);
  not not_4 (not_4_out, B[0]);
  not not_5 (not_5_out, A[1]);
  not not_6 (not_6_out, A[0]);
  not not_7 (not_7_out, A[1]);
  not not_8 (not_8_out, A[0]);
  xnor xnor_1 (xnor_1_out, A[0], B[0]);
  xnor xnor_2 (xnor_2_out, A[1], B[1]);
  xor xor_1 (xor_1_out, A[0], B[0]);
  xor xor_2 (xor_2_out, A[1], B[1]);
  and and_1 (and_1_out, A[1], not_1_out);
  and and_2 (and_2_out, A[0], not_2_out, not_3_out);
  and and_3 (and_3_out, A[0], A[1], not_4_out);
  and and_4 (and_4_out, not_5_out, B[1]);
  and and_5 (and_5_out, not_6_out, not_7_out, B[0]);
  and and_6 (and_6_out, not_8_out, B[0], B[1]);
  and and_7 (Y_same, xnor_1_out, xnor_2_out);
  or or_1 (Y_notsame, xor_1_out, xor_2_out);
  or or_2 (Y_abt, and_1_out, and_2_out, and_3_out);
  or or_3 (Y_alt, and_4_out, and_5_out, and_6_out);
endmodule

module encode_8to3 (
  input  D7,
  input  D6,
  input  D5,
  input  D4,
  input  D3,
  input  D2,
  input  D1,
  input  D0,
  output Y2,
  output Y1,
  output Y0
);

  or or_1 (Y2, D4, D5, D6, D7);
  or or_2 (Y1, D2, D3, D6, D7);
  or or_3 (Y0, D1, D3, D5, D7);
endmodule

module decode_3to8 (
  input  D2,
  input  D1,
  input  D0,
  output Y0,
  output Y1,
  output Y2,
  output Y3,
  output Y4,
  output Y5,
  output Y6,
  output Y7
);

  wire not_1_out, not_2_out, not_3_out;

  not not_1 (not_1_out, D2);
  not not_2 (not_2_out, D1);
  not not_3 (not_3_out, D0);
  and and_1 (Y0, not_3_out, not_2_out, not_1_out);
  and and_2 (Y1, D0, not_2_out, not_1_out);
  and and_3 (Y2, not_3_out, D1, not_1_out);
  and and_4 (Y3, D0, D1, not_1_out);
  and and_5 (Y4, not_3_out, not_2_out, D2);
  and and_6 (Y5, D0, not_2_out, D2);
  and and_7 (Y6, not_3_out, D1, D2);
  and and_8 (Y7, D0, D1, D2);
endmodule

module Mux (
  input  IN0,
  input  IN1,
  input  IN2,
  input  IN3,
  input  S1,
  input  S0,
  output Y
);

  wire and_1_out, and_2_out, and_3_out, and_4_out, not_1_out, not_2_out;

  not not_1 (not_1_out, S1);
  not not_2 (not_2_out, S0);
  and and_1 (and_1_out, IN0, not_1_out, not_2_out);
  and and_2 (and_2_out, IN1, not_1_out, S0);
  and and_3 (and_3_out, IN2, S1, not_2_out);
  and and_4 (and_4_out, IN3, S1, S0);
  or or_1 (Y, and_1_out, and_2_out, and_3_out, and_4_out);
endmodule

module DeMux (
  input  Data,
  input  S1,
  input  S0,
  output Out0,
  output Out1,
  output Out2,
  output Out3
);

  wire not_1_out, not_2_out;

  not not_1 (not_1_out, S1);
  not not_2 (not_2_out, S0);
  and and_1 (Out0, Data, not_1_out, not_2_out);
  and and_2 (Out1, Data, not_1_out, S0);
  and and_3 (Out2, Data, S1, not_2_out);
  and and_4 (Out3, Data, S1, S0);
endmodule

module ParityCheck (
  input  A0,
  input  A1,
  input  A2,
  input  B0,
  input  B1,
  input  B2,
  output PE,
  output PO
);

  wire xor_1_out, xor_2_out, xor_4_out;

  xor xor_1 (xor_1_out, A0, A1);
  xor xor_2 (xor_2_out, B0, B1);
  xor xor_3 (PE, xor_1_out, A2);
  xor xor_4 (xor_4_out, xor_2_out, B2);
  not not_1 (PO, xor_4_out);

  // Notes on the sheet:
  //   짝수패리티체커
  //   홀수패리티체커
endmodule

module latchRS (
  input  in_1,
  input  R,
  input  in_3,
  input  in_4,
  input  S,
  output out_6,
  output Q,
  output out_8,
  output Qbar
);

  wire and_1_out, and_2_out;

  nor nor_1 (Q, R, Qbar);
  nor nor_2 (Qbar, Q, S);
  and and_1 (and_1_out, in_1, in_3);
  and and_2 (and_2_out, in_3, in_4);
  nor nor_3 (out_6, and_1_out, out_8);
  nor nor_4 (out_8, out_6, and_2_out);
endmodule

module JK (
  input  J,
  input  K,
  output Q,
  output Qbar
);

  wire and_1_out, and_2_out, and_3_out, and_4_out, CLK_out, nor_1_out, nor_2_out, not_1_out;

  Clock CLK (.out(CLK_out));
  and and_1 (and_1_out, Qbar, J, CLK_out);
  and and_2 (and_2_out, CLK_out, K, Q);
  not not_1 (not_1_out, CLK_out);
  nor nor_1 (nor_1_out, and_1_out, nor_2_out);
  nor nor_2 (nor_2_out, nor_1_out, and_2_out);
  and and_3 (and_3_out, nor_1_out, not_1_out);
  and and_4 (and_4_out, not_1_out, nor_2_out);
  nor nor_3 (Q, and_3_out, Qbar);
  nor nor_4 (Qbar, Q, and_4_out);
endmodule

module T (
  input  J,
  output Q,
  output Qbar
);

  wire and_1_out, and_2_out, and_3_out, and_4_out, CLK_out, nor_1_out, nor_2_out, not_1_out;

  Clock #(.phaseOffset(1)) CLK (.out(CLK_out));
  and and_1 (and_1_out, Qbar, J, CLK_out);
  and and_2 (and_2_out, CLK_out, J, Q);
  not not_1 (not_1_out, CLK_out);
  nor nor_1 (nor_1_out, and_1_out, nor_2_out);
  nor nor_2 (nor_2_out, nor_1_out, and_2_out);
  and and_3 (and_3_out, nor_1_out, not_1_out);
  and and_4 (and_4_out, not_1_out, nor_2_out);
  nor nor_3 (Q, and_3_out, Qbar);
  nor nor_4 (Qbar, Q, and_4_out);
endmodule

module D (
  input  J,
  output Q,
  output Qbar
);

  wire and_1_out, and_2_out, and_3_out, and_4_out, CLK_out, nor_1_out, nor_2_out, not_1_out, not_2_out;

  Clock #(.phaseOffset(1)) CLK (.out(CLK_out));
  not not_1 (not_1_out, J);
  and and_1 (and_1_out, Qbar, J, CLK_out);
  and and_2 (and_2_out, CLK_out, not_1_out, Q);
  not not_2 (not_2_out, CLK_out);
  nor nor_1 (nor_1_out, and_1_out, nor_2_out);
  nor nor_2 (nor_2_out, nor_1_out, and_2_out);
  and and_3 (and_3_out, nor_1_out, not_2_out);
  and and_4 (and_4_out, not_2_out, nor_2_out);
  nor nor_3 (Q, and_3_out, Qbar);
  nor nor_4 (Qbar, Q, and_4_out);
endmodule
