// Logisim project JOB_2000.circ as structural Verilog
module register_siso (
  input  IN_DATA,
  input  CLK,
  output OUT_DATA
);

  wire d_ff_1_q, d_ff_2_q, d_ff_3_q;

  Clock CLKp ();  // open: out
  D_Flip_Flop #(.trigger("falling")) d_ff_1 (.D(IN_DATA), .clk(CLK), .Q(d_ff_1_q));  // open: Qn, preset, reset
  D_Flip_Flop #(.trigger("falling")) d_ff_2 (.D(d_ff_1_q), .clk(CLK), .Q(d_ff_2_q));  // open: Qn, preset, reset
  D_Flip_Flop #(.trigger("falling")) d_ff_3 (.D(d_ff_2_q), .clk(CLK), .Q(d_ff_3_q));  // open: Qn, preset, reset
  D_Flip_Flop #(.trigger("falling")) d_ff_4 (.D(d_ff_3_q), .clk(CLK), .Q(OUT_DATA));  // open: Qn, preset, reset
endmodule

module register_sipo (
  input  IN_DATA,
  input  CLK,
  output OUT_0,
  output OUT_1,
  output OUT_2,
  output OUT_3
);

  Clock CLKp ();  // open: out
  D_Flip_Flop #(.trigger("falling")) d_ff_1 (.D(IN_DATA), .clk(CLK), .Q(OUT_0));  // open: Qn, preset, reset
  D_Flip_Flop #(.trigger("falling")) d_ff_2 (.D(OUT_0), .clk(CLK), .Q(OUT_1));  // open: Qn, preset, reset
  D_Flip_Flop #(.trigger("falling")) d_ff_3 (.D(OUT_1), .clk(CLK), .Q(OUT_2));  // open: Qn, preset, reset
  D_Flip_Flop #(.trigger("falling")) d_ff_4 (.D(OUT_2), .clk(CLK), .Q(OUT_3));  // open: Qn, preset, reset
endmodule

module register_piso (
  input  IN_0,
  input  IN_1,
  input  IN_2,
  input  IN_3,
  input  SHIFT_LOADbar,
  input  CLK,
  output OUT_DATA
);

  wire and_1_out, and_2_out, and_3_out, and_4_out, and_5_out, and_6_out, d_ff_1_q, d_ff_2_q, d_ff_3_q,
       not_1_out, or_1_out, or_2_out, or_3_out;

  Clock CLKp ();  // open: out
  not not_1 (not_1_out, SHIFT_LOADbar);
  D_Flip_Flop #(.trigger("falling")) d_ff_1 (.D(IN_0), .clk(CLK), .Q(d_ff_1_q));  // open: Qn, preset, reset
  and and_1 (and_1_out, d_ff_1_q, SHIFT_LOADbar);
  and and_2 (and_2_out, not_1_out, IN_1);
  or or_1 (or_1_out, and_1_out, and_2_out);
  D_Flip_Flop #(.trigger("falling")) d_ff_2 (.D(or_1_out), .clk(CLK), .Q(d_ff_2_q));  // open: Qn, preset, reset
  and and_3 (and_3_out, d_ff_2_q, SHIFT_LOADbar);
  and and_4 (and_4_out, not_1_out, IN_2);
  or or_2 (or_2_out, and_3_out, and_4_out);
  D_Flip_Flop #(.trigger("falling")) d_ff_3 (.D(or_2_out), .clk(CLK), .Q(d_ff_3_q));  // open: Qn, preset, reset
  and and_5 (and_5_out, d_ff_3_q, SHIFT_LOADbar);
  and and_6 (and_6_out, not_1_out, IN_3);
  or or_3 (or_3_out, and_5_out, and_6_out);
  D_Flip_Flop #(.trigger("falling")) d_ff_4 (.D(or_3_out), .clk(CLK), .Q(OUT_DATA));  // open: Qn, preset, reset
endmodule

module register_pipo (
  input  IN_0,
  input  IN_1,
  input  IN_2,
  input  IN_3,
  input  CLK,
  output OUT_0,
  output OUT_1,
  output OUT_2,
  output OUT_3
);

  Clock CLKp ();  // open: out
  D_Flip_Flop #(.trigger("falling")) d_ff_1 (.D(IN_0), .clk(CLK), .Q(OUT_0));  // open: Qn, preset, reset
  D_Flip_Flop #(.trigger("falling")) d_ff_2 (.D(IN_1), .clk(CLK), .Q(OUT_1));  // open: Qn, preset, reset
  D_Flip_Flop #(.trigger("falling")) d_ff_3 (.D(IN_2), .clk(CLK), .Q(OUT_2));  // open: Qn, preset, reset
  D_Flip_Flop #(.trigger("falling")) d_ff_4 (.D(IN_3), .clk(CLK), .Q(OUT_3));  // open: Qn, preset, reset
endmodule

module register_siso_recirc (
  input  control,
  input  IN_DATA,
  input  CLK,
  output OUT_DATA
);

  wire and_1_out, and_2_out, d_ff_1_q, d_ff_2_q, d_ff_3_q, not_1_out, or_1_out;

  not not_1 (not_1_out, control);
  Clock CLKp ();  // open: out
  and and_1 (and_1_out, OUT_DATA, not_1_out);
  and and_2 (and_2_out, control, IN_DATA);
  D_Flip_Flop #(.trigger("falling")) d_ff_1 (.D(or_1_out), .clk(CLK), .Q(d_ff_1_q));  // open: Qn, preset, reset
  or or_1 (or_1_out, and_1_out, and_2_out);
  D_Flip_Flop #(.trigger("falling")) d_ff_2 (.D(d_ff_1_q), .clk(CLK), .Q(d_ff_2_q));  // open: Qn, preset, reset
  D_Flip_Flop #(.trigger("falling")) d_ff_3 (.D(d_ff_2_q), .clk(CLK), .Q(d_ff_3_q));  // open: Qn, preset, reset
  D_Flip_Flop #(.trigger("falling")) d_ff_4 (.D(d_ff_3_q), .clk(CLK), .Q(OUT_DATA));  // open: Qn, preset, reset

  // Notes on the sheet:
  //   1_high = 직렬 데이터 입력
  //   0_low = 재순환 데이터
endmodule

module select_MUX_2 (
  input  SLI,
  input  SRI,
  input  right_leftbar,
  output Y
);

  wire and_1_out, and_2_out, not_1_out;

  not not_1 (not_1_out, right_leftbar);
  and and_1 (and_1_out, SLI, not_1_out);
  and and_2 (and_2_out, right_leftbar, SRI);
  or or_1 (Y, and_1_out, and_2_out);
endmodule

module register_dual_RL_shift (
  input  SLI,
  input  SRI,
  input  CLK,
  input  R_L,
  output OUT_0,
  output OUT_1,
  output OUT_2,
  output OUT_3,
  output SLO,
  output SRO
);

  wire select_mux_2_1_y, select_mux_2_2_y, select_mux_2_3_y, select_mux_2_4_y;

  select_MUX_2 select_mux_2_1 (.SLI(OUT_1), .SRI(SRI), .right_leftbar(R_L), .Y(select_mux_2_1_y));
  D_Flip_Flop #(.trigger("falling")) d_ff_1 (.D(select_mux_2_1_y), .clk(CLK), .Q(OUT_0));  // open: Qn, preset, reset
  select_MUX_2 select_mux_2_2 (.SLI(OUT_2), .SRI(OUT_0), .right_leftbar(R_L), .Y(select_mux_2_2_y));
  D_Flip_Flop #(.trigger("falling")) d_ff_2 (.D(select_mux_2_2_y), .clk(CLK), .Q(OUT_1));  // open: Qn, preset, reset
  select_MUX_2 select_mux_2_3 (.SLI(OUT_3), .SRI(OUT_1), .right_leftbar(R_L), .Y(select_mux_2_3_y));
  D_Flip_Flop #(.trigger("falling")) d_ff_3 (.D(select_mux_2_3_y), .clk(CLK), .Q(OUT_2));  // open: Qn, preset, reset
  select_MUX_2 select_mux_2_4 (.SLI(SLI), .SRI(OUT_2), .right_leftbar(R_L), .Y(select_mux_2_4_y));
  D_Flip_Flop #(.trigger("falling")) d_ff_4 (.D(select_mux_2_4_y), .clk(CLK), .Q(OUT_3));  // open: Qn, preset, reset

  assign SLO = OUT_0;
  assign SRO = OUT_3;

  // Notes on the sheet:
  //   1:Right
  //   0:Left
endmodule
