// Logisim project JOB_3000.circ as structural Verilog
module main (
  input  CLK,
  input  Clear,
  output Y_0,
  output Y_1,
  output Y_2,
  output Y_3
);

  D_Flip_Flop d_ff_1 (.D(Y_3), .clk(CLK), .Q(Y_0), .preset(Clear), .reset(Clear));  // open: Qn
  D_Flip_Flop d_ff_2 (.D(Y_0), .clk(CLK), .Q(Y_1));  // open: Qn, preset, reset
  D_Flip_Flop d_ff_3 (.D(Y_1), .clk(CLK), .Q(Y_2));  // open: Qn, preset, reset
  D_Flip_Flop d_ff_4 (.D(Y_2), .clk(CLK), .Q(Y_3));  // open: Qn, preset, reset
endmodule

module counter_async_up_4bits (
  input  CLK,
  output Y_0,
  output Y_1,
  output Y_2,
  output Y_3
);

  J_K_Flip_Flop #(.trigger("falling")) j_k_ff_1 (.J(1'b1), .K(1'b1), .clk(CLK), .Q(Y_0));  // open: Qn, preset, reset
  J_K_Flip_Flop #(.trigger("falling")) j_k_ff_2 (.J(1'b1), .K(1'b1), .clk(Y_0), .Q(Y_1));  // open: Qn, preset, reset
  J_K_Flip_Flop #(.trigger("falling")) j_k_ff_3 (.J(1'b1), .K(1'b1), .clk(Y_1), .Q(Y_2));  // open: Qn, preset, reset
  J_K_Flip_Flop #(.trigger("falling")) j_k_ff_4 (.J(1'b1), .K(1'b1), .clk(Y_2), .Q(Y_3));  // open: Qn, preset, reset
endmodule

module counter_async_down_4bits (
  input  CLK,
  output Y_0,
  output Y_1,
  output Y_2,
  output Y_3
);

  wire j_k_ff_1_q, j_k_ff_2_q, j_k_ff_3_q;

  J_K_Flip_Flop #(.trigger("falling")) j_k_ff_1 (
    .J(1'b1), .K(1'b1), .clk(CLK), .Q(j_k_ff_1_q), .Qn(Y_0));  // open: preset, reset
  J_K_Flip_Flop #(.trigger("falling")) j_k_ff_2 (
    .J(1'b1), .K(1'b1), .clk(j_k_ff_1_q), .Q(j_k_ff_2_q), .Qn(Y_1));  // open: preset, reset
  J_K_Flip_Flop #(.trigger("falling")) j_k_ff_3 (
    .J(1'b1), .K(1'b1), .clk(j_k_ff_2_q), .Q(j_k_ff_3_q), .Qn(Y_2));  // open: preset, reset
  J_K_Flip_Flop #(.trigger("falling")) j_k_ff_4 (
    .J(1'b1), .K(1'b1), .clk(j_k_ff_3_q), .Qn(Y_3));  // open: Q, preset, reset
endmodule

module counter_sync_3bits (
  input  CLK,
  output Y_0,
  output Y_1,
  output Y_2
);

  wire and_1_out;

  J_K_Flip_Flop #(.trigger("falling")) j_k_ff_1 (.J(1'b1), .K(1'b1), .clk(CLK), .Q(Y_0));  // open: Qn, preset, reset
  J_K_Flip_Flop #(.trigger("falling")) j_k_ff_2 (.J(Y_0), .K(Y_0), .clk(CLK), .Q(Y_1));  // open: Qn, preset, reset
  and and_1 (and_1_out, Y_0, Y_1);
  J_K_Flip_Flop #(.trigger("falling")) j_k_ff_3 (
    .J(and_1_out), .K(and_1_out), .clk(CLK), .Q(Y_2));  // open: Qn, preset, reset
endmodule
